# Fritzing sketch RX-WirelessTracker (saved by Fritzing 0.9.5d)

parts:
  A1 = Heltec Wireless Tracker
  microSD1 = MicroSD Card Module

nets:
  N1: A1.Pin_1, microSD1.VCC
  N2: A1.Pin_2, microSD1.GND
  N3: A1.Pin_17, microSD1.CS
  N4: A1.Pin_31, microSD1.SCK
  N5: A1.Pin_32, microSD1.MOSI
  N6: A1.Pin_33, microSD1.MISO

custom parts:
  Heltec Wireless Tracker: The Wireless Tracker card from Heltec.
