# Fritzing sketch TX-WirelessTracker-Apart (saved by Fritzing 0.9.5d)

parts:
  A1 = Heltec Wireless Tracker
  Composant1 = Adafruit Precision 9-DoF LSM6DSOX + LIS3MDL FeatherWing [part_number="Adafruit #4565"]
  Composant2 = Adafruit Feather M0 Adalogger [part_number="Adafruit #2796"]
  microSD1 = MicroSD Card Module
  Composant3 = Arduino Nano (Rev3.0)
  microSD2 = MicroSD Card Module
  R1 = Slide Potentiometer [maximum_resistance=100kΩ]
  Composant4 = Barometric Pressure Sensor - BMP180 Breakout (GY-68)
  LSM6DSOX1 = Adafruit_LSM6DSOX
  Composant5 = Adafruit LSM6DSO32

nets:
  VCC: A1.Pin_1, microSD1.VCC, LSM6DSOX1.VCC
  GND: A1.Pin_2, A1.Pin_8, microSD1.GND, LSM6DSOX1.GND
  N1: A1.Pin_31, microSD1.SCK
  N2: A1.Pin_32, microSD1.MOSI
  N3: A1.Pin_33, microSD1.MISO
  N4: A1.Pin_39, microSD1.CS
  GND_2: Composant1.GND, Composant2.GND, Composant5.GND
  N5: Composant1.SCL, Composant2.SCL, Composant5.SCL
  N6: Composant1.SDA, Composant2.SDA, Composant5.SDA
  3.3V: Composant1.3.3V, Composant2.+3V3, Composant5.3.3V
  N7: Composant3.D10, microSD2.CS
  N8: Composant3.D11/MOSI, microSD2.MOSI
  N9: Composant3.D12/MISO, microSD2.MISO
  GND_3: Composant3.GND, microSD2.GND, R1.wiper, Composant4.GND
  VCC_2: Composant3.5V, microSD2.VCC, R1.leg2, Composant4.VCC
  N10: Composant3.A5, Composant4.SCL
  N11: Composant3.A4, Composant4.SDA
  N12: Composant3.A0, R1.leg1
  N13: Composant3.3V3, microSD2.SCK

custom parts:
  Heltec Wireless Tracker: The Wireless Tracker card from Heltec.
  Adafruit Precision 9-DoF LSM6DSOX + LIS3MDL FeatherWing: Upgrade any Feather board with precision motion sensing with the ST 9-DoF IMU, an all-in-one sensing 'Wing. It sports two fantastic sensors from ST to provide 9 degrees of full-motion data. The board includes an LSM6DSOX, a 6-DoF IMU accelerometer + gyro. The 3-axis accelerometer can tell you which direction is down towards the Earth (by measuring gravity) or how fast the board is accelerating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
  Adafruit Feather M0 Adalogger: This is the Adafruit Feather M0 Adalogger - our take on an 'all-in-one' Cortex M0 datalogger (or data-reader) with built in USB and battery charging. Its an Adafruit Feather M0 with a microSD holder ready to rock! We have other boards in the Feather family, check'em out here At the Feather M0's heart is an ATSAMD21G18 ARM Cortex M0 processor, clocked at 48 MHz and at 3.3V logic, the same one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
